# Fritzing sketch Sketch OLED CLock (saved by Fritzing 0.9.2b)

parts:
  U1 = ESP8266 NodeMCU LoLin module
  OLED_I2C1 = OLED 128x64 I2C Monochrome Display

nets:
  N1: U1.D1, OLED_I2C1.SCK
  N2: U1.D2, OLED_I2C1.SDA
  3V3: U1.3V3, OLED_I2C1.VDD
  GND: U1.GND, OLED_I2C1.GND

custom parts:
  ESP8266 NodeMCU LoLin module: ESP8266 based NodeMCU
